# Fritzing sketch Conservation of mechanical energy (saved by Fritzing 0.9.3b)
breadboards: 1

parts:
  Componente1 = Arduino Uno (Rev3)
  U1 = LCD-16X2 [package=lcd-16x2_noholes]  # not connected
  R1 = TRIMPOT [package=3362u-2]
  R2 = Resistor [tolerance=±5% resistance=220 package=THT]
  S1 = Momentary Switch [package=ksa_sealed_tac_switch]
  S2 = Pushbutton [package="[SMD]"]
  hc-sr1 = hc-sr04
  hc-sr2 = hc-sr04

nets:
  N1: Componente1.D8, S1.1
  N2: Componente1.D9_PWM, S2.Pin_1, S2.Pin_2
  N3: Componente1.D13/SCK, hc-sr2.Echo
  N4: Componente1.D6_PWM, hc-sr1.Trig, hc-sr2.Trig
  N5: Componente1.D7, hc-sr1.Echo
  VCC: Componente1.5V, R1.CW, R2.Pin_0, hc-sr1.VCC, hc-sr2.VCC
  GND: Componente1.GND, R1.CCW, S1.3, S2.Pin_3, S2.Pin_4, hc-sr1.GND, hc-sr2.GND

notes:
  Cm
  Cm2
